// Logisim project sum_knf.circ as structural Verilog: 2 circuits, main circuit main
module main (
  input  [7:0] number1,
  input  [7:0] number2,
  output [7:0] sum
);

  wire sknf_summator_1_p, sknf_summator_2_p, sknf_summator_3_p, sknf_summator_4_p, sknf_summator_5_p,
       sknf_summator_6_p, sknf_summator_7_p, sknf_summator_8_p;

  // Probe on number2
  // Probe on number1
  sknf_summator sknf_summator_1 (
    .x3(sknf_summator_8_p), .x1(number1[0]), .x2(number2[0]), .s(sum[0]), .p(sknf_summator_1_p));
  sknf_summator sknf_summator_2 (
    .x3(sknf_summator_1_p), .x1(number1[1]), .x2(number2[1]), .s(sum[1]), .p(sknf_summator_2_p));
  sknf_summator sknf_summator_3 (
    .x3(sknf_summator_2_p), .x1(number1[2]), .x2(number2[2]), .s(sum[2]), .p(sknf_summator_3_p));
  sknf_summator sknf_summator_4 (
    .x3(sknf_summator_3_p), .x1(number1[3]), .x2(number2[3]), .s(sum[3]), .p(sknf_summator_4_p));
  sknf_summator sknf_summator_5 (
    .x3(sknf_summator_4_p), .x1(number1[4]), .x2(number2[4]), .s(sum[4]), .p(sknf_summator_5_p));
  sknf_summator sknf_summator_6 (
    .x3(sknf_summator_5_p), .x1(number1[5]), .x2(number2[5]), .s(sum[5]), .p(sknf_summator_6_p));
  sknf_summator sknf_summator_7 (
    .x3(sknf_summator_6_p), .x1(number1[6]), .x2(number2[6]), .s(sum[6]), .p(sknf_summator_7_p));
  sknf_summator sknf_summator_8 (
    .x3(sknf_summator_7_p), .x1(number1[7]), .x2(number2[7]), .s(sum[7]), .p(sknf_summator_8_p));
  // Probe on sum
endmodule

module sknf_summator (
  input  x3,
  input  x1,
  input  x2,
  output s,
  output p
);

  wire not_1_out, not_2_out, not_3_out, or_1_out, or_2_out, or_3_out, or_4_out, or_5_out, or_6_out, or_7_out;

  not not_1 (not_1_out, x1);
  not not_2 (not_2_out, x2);
  not not_3 (not_3_out, x3);
  or or_1 (or_1_out, x1, x2);
  or or_2 (or_2_out, x2, x3);
  or or_3 (or_3_out, x1, x3);
  or or_4 (or_4_out, x1, x2, x3);
  or or_5 (or_5_out, x1, not_2_out, not_3_out);
  or or_6 (or_6_out, not_1_out, x2, not_3_out);
  or or_7 (or_7_out, not_1_out, not_2_out, x3);
  and and_1 (p, or_1_out, or_2_out, or_3_out);
  and and_2 (s, or_4_out, or_5_out, or_6_out, or_7_out);

  // Notes on the sheet:
  //   x2: pull=up
endmodule
