// Logisim project task_2.circ as structural Verilog: 1 circuit, main circuit main
module main (
  input  x4,
  input  x3,
  input  x2,
  input  x1,
  output y4,
  output y3,
  output y2,
  output y1
);

  wire and_1_out, and_2_out, and_3_out, and_4_out, and_5_out, and_6_out, and_7_out, and_8_out, and_9_out,
       and_10_out, not_1_out, not_2_out, not_3_out;

  not not_1 (not_1_out, x3);
  not not_2 (not_2_out, x2);
  not not_3 (not_3_out, x1);
  and and_1 (and_1_out, x2, x1);
  and and_2 (and_2_out, not_1_out, not_3_out);
  and and_3 (and_3_out, not_1_out, not_2_out);
  and and_4 (and_4_out, x3, x2, x1);
  and and_5 (and_5_out, not_2_out, x1);
  and and_6 (and_6_out, x2, not_3_out);
  and and_7 (and_7_out, x4, x3);
  and and_8 (and_8_out, x4, x1);
  and and_9 (and_9_out, x4, x2);
  and and_10 (and_10_out, x3, x4);
  or or_1 (y4, x4, x3, and_1_out);
  or or_2 (y3, and_2_out, and_3_out, and_4_out, x4);
  or or_3 (y2, and_5_out, and_6_out, and_7_out, and_8_out);
  or or_4 (y1, and_9_out, not_3_out, and_10_out);
endmodule
