// Logisim project lr5.circ as structural Verilog: 1 circuit, main circuit main
module main (
  input  V,
  output z1,
  output z2,
  output z3
);

  wire and_1_out, and_2_out, clock_1_out;

  Clock clock_1 (.out(clock_1_out));
  and and_1 (and_1_out, z1, V);
  and and_2 (and_2_out, z2, z1, V);
  T_Flip_Flop T1 (.T(V), .clk(clock_1_out), .Q(z1));  // open: Qn, reset, preset
  T_Flip_Flop T2 (.T(and_1_out), .clk(clock_1_out), .Q(z2));  // open: Qn, reset, preset
  T_Flip_Flop T3 (.T(and_2_out), .clk(clock_1_out), .Q(z3));  // open: Qn, reset, preset
endmodule
